// Logisim project Ripple_Carry_Adder.circ as structural Verilog: 4 circuits, main circuit main
module main (
  input  a_3,
  input  b_3,
  input  a_2,
  input  b_2,
  input  a_1,
  input  b_1,
  input  a_0,
  input  b_0,
  input  c_0,
  output c_4,
  output s_3,
  output s_2,
  output s_1,
  output s_0
);

  wire _0_Bit_out_4, _1_bit_out_4, _2_bit_out_4;

  _1bit_adder _3_bit (.out_4(c_4), .in_1(a_3), .in_2(b_3), .out_5(s_3), .in_3(_2_bit_out_4));
  _1bit_adder _2_bit (.out_4(_2_bit_out_4), .in_1(a_2), .in_2(b_2), .out_5(s_2), .in_3(_1_bit_out_4));
  _1bit_adder _1_bit (.out_4(_1_bit_out_4), .in_1(a_1), .in_2(b_1), .out_5(s_1), .in_3(_0_Bit_out_4));
  _1bit_adder _0_Bit (.out_4(_0_Bit_out_4), .in_1(a_0), .in_2(b_0), .out_5(s_0), .in_3(c_0));

  // Notes on the sheet:
  //   Made by cs1221596 and cs1221094
endmodule

module xor_gate (
  input  in_1,
  input  in_2,
  output out_3
);

  wire and_1_out, and_2_out, not_1_out, not_2_out;

  not not_1 (not_1_out, in_1);
  not not_2 (not_2_out, in_2);
  and and_1 (and_1_out, not_1_out, in_2);
  and and_2 (and_2_out, in_1, not_2_out);
  or or_1 (out_3, and_1_out, and_2_out);
endmodule

module _1bit_adder (
  input  in_1,
  input  in_2,
  input  in_3,
  output out_4,
  output out_5
);

  wire and_1_out, and_2_out, xor_gate_1_out_3;

  or or_1 (out_4, and_1_out, and_2_out);
  and and_1 (and_1_out, xor_gate_1_out_3, in_3);
  and and_2 (and_2_out, in_1, in_2);
  xor_gate xor_gate_1 (.in_1(in_2), .in_2(in_1), .out_3(xor_gate_1_out_3));
  xor_gate xor_gate_2 (.in_1(in_3), .in_2(xor_gate_1_out_3), .out_3(out_5));
endmodule

module simulation (
);

  main main_1 ();  // open: c_4, a_3, b_3, a_2, b_2, a_1, b_1, a_0, b_0, s_3, s_2, s_1, s_0, c_0
endmodule
