// Logisim project alu.circ as structural Verilog: 20 circuits, main circuit main
module main (
  input  [31:0] A,
  input  [31:0] B,
  input  [3:0] ALUSel,
  output overflow,
  output zero,
  output [31:0] Result
);

  control_signal control_signal_1 (
    .in_1(A), .in_2(B), .ALUSel(ALUSel), .overflow(overflow), .zero(zero), .Result(Result));

  // Notes on the sheet:
  //   cs1221596 and cs1221094
endmodule

module add_0 (
  input  [30:0] A_30_0,
  input  [30:0] B_30_0,
  input  A_31,
  input  B_31,
  output [31:0] Result,
  output Overflow
);

  wire [31:0] bit_extender_1_out, bit_extender_2_out;

  assign bit_extender_1_out = {{1{A_31}}, A_30_0};  // Bit_Extender bit_extender_1
  assign bit_extender_2_out = {{1{B_31}}, B_30_0};  // Bit_Extender bit_extender_2
  Adder #(.width(32)) adder_1 (
    .a(bit_extender_1_out), .b(bit_extender_2_out), .out(Result), .cin(1'b0), .cout(Overflow));
endmodule

module sll_1 (
  input  [30:0] A_30_0,
  input  [30:0] B_30_0,
  input  A_31,
  input  B_31,
  output [31:0] Result
);

  wire bitfinder_1_found;
  wire [4:0] bitselector_1_out;
  wire [31:0] bit_extender_1_out, bit_extender_2_out, shifter_1_out;

  assign bit_extender_1_out = {{1{A_31}}, A_30_0};  // Bit_Extender bit_extender_1
  assign bit_extender_2_out = {{1{B_31}}, B_30_0};  // Bit_Extender bit_extender_2
  BitSelector #(.width(32), .group(5)) bitselector_1 (.in(bit_extender_2_out), .out(bitselector_1_out), .sel(3'b000));
  BitFinder #(.width(27)) bitfinder_1 (.in(bit_extender_2_out[31:5]), .found(bitfinder_1_found));  // open: index
  Shifter #(.width(32)) shifter_1 (.in(bit_extender_1_out), .\dist (bitselector_1_out), .out(shifter_1_out));
  MUX_32bit_2_1 mux_32bit_2_1_1 (.in_1(shifter_1_out), .in_2({32{1'b0}}), .in_3(bitfinder_1_found), .out_4(Result));
endmodule

module slt_2 (
  input  [30:0] A_30_0,
  input  [30:0] B_30_0,
  input  A_31,
  input  B_31,
  output [31:0] Result
);

  wire comparator_1_lt;
  wire [31:0] bit_extender_1_out, bit_extender_2_out;

  assign bit_extender_1_out = {{1{A_31}}, A_30_0};  // Bit_Extender bit_extender_1
  assign bit_extender_2_out = {{1{B_31}}, B_30_0};  // Bit_Extender bit_extender_2
  Comparator #(.width(32)) comparator_1 (
    .a(bit_extender_1_out), .b(bit_extender_2_out), .lt(comparator_1_lt));  // open: gt, eq
  assign Result = {{31{1'b0}}, comparator_1_lt};  // Bit_Extender bit_extender_3
endmodule

module xor_4 (
  input  [30:0] A_30_0,
  input  [30:0] B_30_0,
  input  A_31,
  input  B_31,
  output [31:0] Result
);

  wire [31:0] bit_extender_1_out, bit_extender_2_out;

  assign bit_extender_1_out = {{1{A_31}}, A_30_0};  // Bit_Extender bit_extender_1
  assign bit_extender_2_out = {{1{B_31}}, B_30_0};  // Bit_Extender bit_extender_2
  assign Result = bit_extender_1_out ^ bit_extender_2_out;  // XOR_Gate xor_1, 32 bits wide
endmodule

module srl_5 (
  input  [30:0] A_30_0,
  input  [30:0] B_30_0,
  input  A_31,
  input  B_31,
  output [31:0] Result
);

  wire bitfinder_1_found;
  wire [4:0] bitselector_1_out;
  wire [31:0] bit_extender_1_out, bit_extender_2_out, shifter_1_out;

  assign bit_extender_1_out = {{1{A_31}}, A_30_0};  // Bit_Extender bit_extender_1
  assign bit_extender_2_out = {{1{B_31}}, B_30_0};  // Bit_Extender bit_extender_2
  Shifter #(.width(32), .shift("lr")) shifter_1 (
    .in(bit_extender_1_out), .\dist (bitselector_1_out), .out(shifter_1_out));
  BitSelector #(.width(32), .group(5)) bitselector_1 (.in(bit_extender_2_out), .out(bitselector_1_out), .sel(3'b000));
  BitFinder #(.width(27)) bitfinder_1 (.in(bit_extender_2_out[31:5]), .found(bitfinder_1_found));  // open: index
  MUX_32bit_2_1 mux_32bit_2_1_1 (.in_1(shifter_1_out), .in_2({32{1'b0}}), .in_3(bitfinder_1_found), .out_4(Result));
endmodule

module or_6 (
  input  [30:0] A_30_0,
  input  [30:0] B_30_0,
  input  A_31,
  input  B_31,
  output [31:0] out_5
);

  wire [31:0] bit_extender_1_out, bit_extender_2_out;

  assign bit_extender_1_out = {{1{A_31}}, A_30_0};  // Bit_Extender bit_extender_1
  assign bit_extender_2_out = {{1{B_31}}, B_30_0};  // Bit_Extender bit_extender_2
  assign out_5 = bit_extender_1_out | bit_extender_2_out;  // OR_Gate or_1, 32 bits wide
endmodule

module and_7 (
  input  [30:0] A_30_0,
  input  [30:0] B_30_0,
  input  A_31,
  input  B_31,
  output [31:0] out_5
);

  wire [31:0] bit_extender_1_out, bit_extender_2_out;

  assign bit_extender_1_out = {{1{A_31}}, A_30_0};  // Bit_Extender bit_extender_1
  assign bit_extender_2_out = {{1{B_31}}, B_30_0};  // Bit_Extender bit_extender_2
  assign out_5 = bit_extender_1_out & bit_extender_2_out;  // AND_Gate and_1, 32 bits wide
endmodule

module mul_8 (
  input  [30:0] A_30_0,
  input  [30:0] B_30_0,
  input  A_31,
  input  B_31,
  output [31:0] Result
);

  wire [31:0] bit_extender_1_out, bit_extender_2_out;

  assign bit_extender_1_out = {{1{A_31}}, A_30_0};  // Bit_Extender bit_extender_1
  assign bit_extender_2_out = {{1{B_31}}, B_30_0};  // Bit_Extender bit_extender_2
  Multiplier #(.width(32)) multiplier_1 (
    .a(bit_extender_1_out), .b(bit_extender_2_out), .out(Result), .cin({32{1'b0}}));  // open: cout
endmodule

module mulh_9 (
  input  [30:0] A_30_0,
  input  [30:0] B_30_0,
  input  A_31,
  input  B_31,
  output [31:0] Result
);

  wire [31:0] bit_extender_1_out, bit_extender_2_out;

  assign bit_extender_1_out = {{1{A_31}}, A_30_0};  // Bit_Extender bit_extender_1
  assign bit_extender_2_out = {{1{B_31}}, B_30_0};  // Bit_Extender bit_extender_2
  Multiplier #(.width(32)) multiplier_1 (
    .a(bit_extender_1_out), .b(bit_extender_2_out), .cin({32{1'b0}}), .cout(Result));  // open: out
endmodule

module sub_12 (
  input  [30:0] A_30_0,
  input  [30:0] B_30_0,
  input  A_31,
  input  B_31,
  output [31:0] Result
);

  wire [31:0] bit_extender_1_out, bit_extender_2_out;

  assign bit_extender_1_out = {{1{A_31}}, A_30_0};  // Bit_Extender bit_extender_1
  assign bit_extender_2_out = {{1{B_31}}, B_30_0};  // Bit_Extender bit_extender_2
  Subtractor #(.width(32)) subtractor_1 (
    .a(bit_extender_1_out), .b(bit_extender_2_out), .out(Result), .bin(1'b0));  // open: bout
endmodule

module sra_13 (
  input  [30:0] A_30_0,
  input  [30:0] B_30_0,
  input  A_31,
  input  B_31,
  output [31:0] Result
);

  wire bitfinder_1_found;
  wire [4:0] bitselector_1_out;
  wire [31:0] bit_extender_1_out, bit_extender_2_out, shifter_1_out;

  assign bit_extender_1_out = {{1{A_31}}, A_30_0};  // Bit_Extender bit_extender_1
  assign bit_extender_2_out = {{1{B_31}}, B_30_0};  // Bit_Extender bit_extender_2
  BitSelector #(.width(32), .group(5)) bitselector_1 (.in(bit_extender_2_out), .out(bitselector_1_out), .sel(3'b000));
  BitFinder #(.width(27)) bitfinder_1 (.in(bit_extender_2_out[31:5]), .found(bitfinder_1_found));  // open: index
  Shifter #(.width(32), .shift("ar")) shifter_1 (
    .in(bit_extender_1_out), .\dist (bitselector_1_out), .out(shifter_1_out));
  MUX_32bit_2_1 mux_32bit_2_1_1 (.in_1(shifter_1_out), .in_2({32{1'b0}}), .in_3(bitfinder_1_found), .out_4(Result));
endmodule

module bsel_15 (
  input  [30:0] A_30_0,
  input  [30:0] B_30_0,
  input  A_31,
  input  B_31,
  output [31:0] Result
);

  assign Result = {{1{B_31}}, B_30_0};  // Bit_Extender bit_extender_1
endmodule

module splitter (
  input  [31:0] A,
  input  [31:0] B,
  output [30:0] A_30_0,
  output [30:0] B_30_0,
  output A_31,
  output B_31
);


  assign A_30_0 = A[30:0];
  assign A_31 = A[31];
  assign B_30_0 = B[30:0];
  assign B_31 = B[31];
endmodule

module MUX_32bit_2_1 (
  input  [31:0] in_1,
  input  [31:0] in_2,
  input  in_3,
  output [31:0] out_4
);

  wire [31:0] and_1_out, and_2_out, bit_extender_1_out, not_1_out;

  assign bit_extender_1_out = {{31{in_3}}, in_3};  // Bit_Extender bit_extender_1
  assign not_1_out = ~bit_extender_1_out;  // NOT_Gate not_1, 32 bits wide
  assign and_1_out = in_1 & not_1_out;  // AND_Gate and_1, 32 bits wide
  assign and_2_out = in_2 & bit_extender_1_out;  // AND_Gate and_2, 32 bits wide
  assign out_4 = and_1_out | and_2_out;  // OR_Gate or_1, 32 bits wide
endmodule

module _2_s_complement (
  input  [30:0] in_1,
  input  in_2,
  output [31:0] out_3
);

  wire [30:0] adder_1_out, bit_extender_1_out, bit_extender_2_out, xor_1_out;

  assign bit_extender_1_out = {{30{in_2}}, in_2};  // Bit_Extender bit_extender_1
  assign bit_extender_2_out = {{30{1'b0}}, in_2};  // Bit_Extender bit_extender_2
  assign xor_1_out = in_1 ^ bit_extender_1_out;  // XOR_Gate xor_1, 31 bits wide
  Adder #(.width(31)) adder_1 (.a(xor_1_out), .b(bit_extender_2_out), .out(adder_1_out), .cin(1'b0));  // open: cout
  assign out_3 = {{1{1'b0}}, adder_1_out};  // Bit_Extender bit_extender_3
endmodule

module MUX_1bit_2_1 (
  input  in_1,
  input  in_2,
  input  in_3,
  output out_4
);

  wire and_1_out, and_2_out, not_1_out;

  not not_1 (not_1_out, in_3);
  and and_1 (and_1_out, in_1, not_1_out);
  and and_2 (and_2_out, in_2, in_3);
  or or_1 (out_4, and_1_out, and_2_out);
endmodule

module mulhu_11 (
  input  [30:0] A_30_0,
  input  [30:0] B_30_0,
  input  A_31,
  input  B_31,
  output [31:0] out_5
);

  wire and_1_out;
  wire [31:0] adder_1_out, adder_2_out, and_2_out, and_3_out, bit_extender_1_out, bit_extender_2_out,
       bit_extender_3_out, bit_extender_4_out, bit_extender_5_out, multiplier_1_cout, shifter_1_out,
       shifter_2_out;

  assign bit_extender_1_out = {{31{A_31}}, A_31};  // Bit_Extender bit_extender_1
  assign bit_extender_2_out = {{31{B_31}}, B_31};  // Bit_Extender bit_extender_2
  and and_1 (and_1_out, A_31, B_31);
  assign bit_extender_3_out = {{1{1'b0}}, A_30_0};  // Bit_Extender bit_extender_3
  assign bit_extender_4_out = {{1{1'b0}}, B_30_0};  // Bit_Extender bit_extender_4
  assign bit_extender_5_out = {{31{1'b0}}, and_1_out};  // Bit_Extender bit_extender_5
  Shifter #(.width(32)) shifter_1 (.in(bit_extender_5_out), .\dist (5'b11110), .out(shifter_1_out));
  Multiplier #(.width(32)) multiplier_1 (
    .a(bit_extender_3_out), .b(bit_extender_4_out), .cin({32{1'b0}}), .cout(multiplier_1_cout));  // open: out
  assign and_2_out = bit_extender_1_out & bit_extender_4_out;  // AND_Gate and_2, 32 bits wide
  assign and_3_out = bit_extender_3_out & bit_extender_2_out;  // AND_Gate and_3, 32 bits wide
  Adder #(.width(32)) adder_1 (.a(and_2_out), .b(and_3_out), .out(adder_1_out));  // open: cin, cout
  Shifter #(.width(32), .shift("lr")) shifter_2 (.in(adder_1_out), .\dist (5'b00001), .out(shifter_2_out));
  Adder #(.width(32)) adder_2 (.a(multiplier_1_cout), .b(shifter_2_out), .out(adder_2_out), .cin(1'b0));  // open: cout
  Adder #(.width(32)) adder_3 (.a(adder_2_out), .b(shifter_1_out), .out(out_5), .cin(1'b0));  // open: cout
endmodule

module MUX_16_1 (
  input  [31:0] _0,
  input  [31:0] _8,
  input  [31:0] _4,
  input  [31:0] _12,
  input  [31:0] _2,
  input  [31:0] _10,
  input  [31:0] _6,
  input  [31:0] _14,
  input  [31:0] _1,
  input  [31:0] _9,
  input  [31:0] _5,
  input  [31:0] _13,
  input  [31:0] _3,
  input  [31:0] _11,
  input  [31:0] _7,
  input  [31:0] _15,
  input  [3:0] in_17,
  output [31:0] out_18
);

  wire [31:0] mux_32bit_2_1_1_out_4, mux_32bit_2_1_2_out_4, mux_32bit_2_1_3_out_4, mux_32bit_2_1_4_out_4,
       mux_32bit_2_1_5_out_4, mux_32bit_2_1_6_out_4, mux_32bit_2_1_7_out_4, mux_32bit_2_1_8_out_4,
       mux_32bit_2_1_9_out_4, mux_32bit_2_1_10_out_4, mux_32bit_2_1_11_out_4, mux_32bit_2_1_12_out_4,
       mux_32bit_2_1_13_out_4, mux_32bit_2_1_14_out_4;

  MUX_32bit_2_1 mux_32bit_2_1_1 (.in_1(_0), .in_2(_8), .in_3(in_17[3]), .out_4(mux_32bit_2_1_1_out_4));
  MUX_32bit_2_1 mux_32bit_2_1_2 (.in_1(_4), .in_2(_12), .in_3(in_17[3]), .out_4(mux_32bit_2_1_2_out_4));
  MUX_32bit_2_1 mux_32bit_2_1_3 (.in_1(_2), .in_2(_10), .in_3(in_17[3]), .out_4(mux_32bit_2_1_3_out_4));
  MUX_32bit_2_1 mux_32bit_2_1_4 (.in_1(_6), .in_2(_14), .in_3(in_17[3]), .out_4(mux_32bit_2_1_4_out_4));
  MUX_32bit_2_1 mux_32bit_2_1_5 (.in_1(_1), .in_2(_9), .in_3(in_17[3]), .out_4(mux_32bit_2_1_5_out_4));
  MUX_32bit_2_1 mux_32bit_2_1_6 (.in_1(_5), .in_2(_13), .in_3(in_17[3]), .out_4(mux_32bit_2_1_6_out_4));
  MUX_32bit_2_1 mux_32bit_2_1_7 (.in_1(_3), .in_2(_11), .in_3(in_17[3]), .out_4(mux_32bit_2_1_7_out_4));
  MUX_32bit_2_1 mux_32bit_2_1_8 (.in_1(_7), .in_2(_15), .in_3(in_17[3]), .out_4(mux_32bit_2_1_8_out_4));
  MUX_32bit_2_1 mux_32bit_2_1_9 (
    .in_1(mux_32bit_2_1_1_out_4), .in_2(mux_32bit_2_1_2_out_4), .in_3(in_17[2]), .out_4(mux_32bit_2_1_9_out_4));
  MUX_32bit_2_1 mux_32bit_2_1_10 (
    .in_1(mux_32bit_2_1_3_out_4), .in_2(mux_32bit_2_1_4_out_4), .in_3(in_17[2]),
    .out_4(mux_32bit_2_1_10_out_4));
  MUX_32bit_2_1 mux_32bit_2_1_11 (
    .in_1(mux_32bit_2_1_5_out_4), .in_2(mux_32bit_2_1_6_out_4), .in_3(in_17[2]),
    .out_4(mux_32bit_2_1_11_out_4));
  MUX_32bit_2_1 mux_32bit_2_1_12 (
    .in_1(mux_32bit_2_1_7_out_4), .in_2(mux_32bit_2_1_8_out_4), .in_3(in_17[2]),
    .out_4(mux_32bit_2_1_12_out_4));
  MUX_32bit_2_1 mux_32bit_2_1_13 (
    .in_1(mux_32bit_2_1_9_out_4), .in_2(mux_32bit_2_1_10_out_4), .in_3(in_17[1]),
    .out_4(mux_32bit_2_1_13_out_4));
  MUX_32bit_2_1 mux_32bit_2_1_14 (
    .in_1(mux_32bit_2_1_11_out_4), .in_2(mux_32bit_2_1_12_out_4), .in_3(in_17[1]),
    .out_4(mux_32bit_2_1_14_out_4));
  MUX_32bit_2_1 mux_32bit_2_1_15 (
    .in_1(mux_32bit_2_1_13_out_4), .in_2(mux_32bit_2_1_14_out_4), .in_3(in_17[0]), .out_4(out_18));
endmodule

module control_signal (
  input  [31:0] in_1,
  input  [31:0] in_2,
  input  [3:0] ALUSel,
  output overflow,
  output zero,
  output [31:0] Result
);

  wire add_0_1_overflow, bitfinder_1_found, not_1_out, splitter_1_a_31, splitter_1_b_31;
  wire [30:0] splitter_1_a_30_0, splitter_1_b_30_0;
  wire [31:0] add_0_1_result, and_7_1_out_5, bsel_15_1_result, mul_8_1_result, mulh_9_1_result,
       mulhu_11_1_out_5, or_6_1_out_5, sll_1_1_result, slt_2_1_result, sra_13_1_result, srl_5_1_result,
       sub_12_1_result, xor_4_1_result;

  splitter splitter_1 (
    .A(in_1), .B(in_2), .A_30_0(splitter_1_a_30_0), .B_30_0(splitter_1_b_30_0), .A_31(splitter_1_a_31),
    .B_31(splitter_1_b_31));
  add_0 add_0_1 (
    .A_30_0(splitter_1_a_30_0), .B_30_0(splitter_1_b_30_0), .A_31(splitter_1_a_31), .B_31(splitter_1_b_31),
    .Overflow(add_0_1_overflow), .Result(add_0_1_result));
  mul_8 mul_8_1 (
    .A_30_0(splitter_1_a_30_0), .B_30_0(splitter_1_b_30_0), .A_31(splitter_1_a_31), .B_31(splitter_1_b_31),
    .Result(mul_8_1_result));
  xor_4 xor_4_1 (
    .A_30_0(splitter_1_a_30_0), .B_30_0(splitter_1_b_30_0), .A_31(splitter_1_a_31), .B_31(splitter_1_b_31),
    .Result(xor_4_1_result));
  sub_12 sub_12_1 (
    .A_30_0(splitter_1_a_30_0), .B_30_0(splitter_1_b_30_0), .A_31(splitter_1_a_31), .B_31(splitter_1_b_31),
    .Result(sub_12_1_result));
  slt_2 slt_2_1 (
    .A_30_0(splitter_1_a_30_0), .B_30_0(splitter_1_b_30_0), .A_31(splitter_1_a_31), .B_31(splitter_1_b_31),
    .Result(slt_2_1_result));
  or_6 or_6_1 (
    .A_30_0(splitter_1_a_30_0), .B_30_0(splitter_1_b_30_0), .A_31(splitter_1_a_31), .B_31(splitter_1_b_31),
    .out_5(or_6_1_out_5));
  sll_1 sll_1_1 (
    .A_30_0(splitter_1_a_30_0), .B_30_0(splitter_1_b_30_0), .A_31(splitter_1_a_31), .B_31(splitter_1_b_31),
    .Result(sll_1_1_result));
  mulh_9 mulh_9_1 (
    .A_30_0(splitter_1_a_30_0), .B_30_0(splitter_1_b_30_0), .A_31(splitter_1_a_31), .B_31(splitter_1_b_31),
    .Result(mulh_9_1_result));
  srl_5 srl_5_1 (
    .A_30_0(splitter_1_a_30_0), .B_30_0(splitter_1_b_30_0), .A_31(splitter_1_a_31), .B_31(splitter_1_b_31),
    .Result(srl_5_1_result));
  sra_13 sra_13_1 (
    .A_30_0(splitter_1_a_30_0), .B_30_0(splitter_1_b_30_0), .A_31(splitter_1_a_31), .B_31(splitter_1_b_31),
    .Result(sra_13_1_result));
  mulhu_11 mulhu_11_1 (
    .A_30_0(splitter_1_a_30_0), .B_30_0(splitter_1_b_30_0), .A_31(splitter_1_a_31), .B_31(splitter_1_b_31),
    .out_5(mulhu_11_1_out_5));
  and_7 and_7_1 (
    .A_30_0(splitter_1_a_30_0), .B_30_0(splitter_1_b_30_0), .A_31(splitter_1_a_31), .B_31(splitter_1_b_31),
    .out_5(and_7_1_out_5));
  bsel_15 bsel_15_1 (
    .A_30_0(splitter_1_a_30_0), .B_30_0(splitter_1_b_30_0), .A_31(splitter_1_a_31), .B_31(splitter_1_b_31),
    .Result(bsel_15_1_result));
  MUX_16_1 mux_16_1_1 (
    ._0(add_0_1_result), ._8(mul_8_1_result), ._4(xor_4_1_result), ._12(sub_12_1_result),
    ._2(slt_2_1_result), ._10({32{1'b0}}), ._6(or_6_1_out_5), ._14({32{1'b0}}), ._1(sll_1_1_result),
    ._9(mulh_9_1_result), ._5(srl_5_1_result), ._13(sra_13_1_result), ._3({32{1'b0}}),
    ._11(mulhu_11_1_out_5), ._7(and_7_1_out_5), ._15(bsel_15_1_result), .in_17(ALUSel), .out_18(Result));
  BitFinder #(.width(4), .\type ("high1")) bitfinder_1 (.in(ALUSel), .found(bitfinder_1_found));  // open: index
  and and_1 (overflow, add_0_1_overflow, not_1_out);
  not not_1 (not_1_out, bitfinder_1_found);
  Comparator #(.width(32)) comparator_1 (.a(Result), .b({32{1'b0}}), .eq(zero));  // open: gt, lt
endmodule
