// Logisim project register.circ as structural Verilog: 1 circuit, main circuit register
// RegWrite
module register (
  input  [4:0] rd,
  input  [31:0] Write_Data,
  input  RegWEn,
  input  [4:0] rs1,
  input  [4:0] rs2,
  output [31:0] Read_Data_1,
  output [31:0] Read_Data_2
);

  wire and_1_out, and_2_out, and_3_out, and_4_out, and_5_out, and_6_out, and_7_out, and_8_out, Clock_out,
       decoder_1_out1, decoder_1_out2, decoder_1_out5, decoder_1_out6, decoder_1_out7, decoder_1_out8,
       decoder_1_out9, decoder_1_out10;
  wire [31:0] x0_q, x1_q, x2_q, x5_q, x6_q, x7_q, x8_q, x9_q, x10_q;

  Decoder #(.select(5), .enable("false")) decoder_1 (
    .out1(decoder_1_out1), .out2(decoder_1_out2), .out5(decoder_1_out5), .out6(decoder_1_out6),
    .out7(decoder_1_out7), .out8(decoder_1_out8), .out9(decoder_1_out9), .out10(decoder_1_out10), .sel(rd));  // open: out0, out3, out4, out11, out12, out13, out14, out15, out16, out17, out18, out19, out20, out21, out22, out23, out24, out25, out26, out27, out28, out29, out30, out31
  and and_1 (and_1_out, RegWEn, decoder_1_out1);
  and and_2 (and_2_out, RegWEn, decoder_1_out2);
  and and_3 (and_3_out, RegWEn, decoder_1_out5);
  and and_4 (and_4_out, RegWEn, decoder_1_out6);
  and and_5 (and_5_out, RegWEn, decoder_1_out7);
  and and_6 (and_6_out, RegWEn, decoder_1_out8);
  and and_7 (and_7_out, RegWEn, decoder_1_out9);
  and and_8 (and_8_out, RegWEn, decoder_1_out10);
  Clock Clock (.out(Clock_out));
  Register #(.width(32)) x0 (.D(Write_Data), .en(1'b0), .Q(x0_q), .clk(Clock_out));  // open: clr
  Register #(.width(32)) x1 (.D(Write_Data), .en(and_1_out), .Q(x1_q), .clk(Clock_out));  // open: clr
  Register #(.width(32)) x2 (.D(Write_Data), .en(and_2_out), .Q(x2_q), .clk(Clock_out));  // open: clr
  Register #(.width(32)) x5 (.D(Write_Data), .en(and_3_out), .Q(x5_q), .clk(Clock_out));  // open: clr
  Register #(.width(32)) x6 (.D(Write_Data), .en(and_4_out), .Q(x6_q), .clk(Clock_out));  // open: clr
  Register #(.width(32)) x7 (.D(Write_Data), .en(and_5_out), .Q(x7_q), .clk(Clock_out));  // open: clr
  Register #(.width(32)) x8 (.D(Write_Data), .en(and_6_out), .Q(x8_q), .clk(Clock_out));  // open: clr
  Register #(.width(32)) x9 (.D(Write_Data), .en(and_7_out), .Q(x9_q), .clk(Clock_out));  // open: clr
  Register #(.width(32)) x10 (.D(Write_Data), .en(and_8_out), .Q(x10_q), .clk(Clock_out));  // open: clr
  Multiplexer #(.select(5), .width(32), .enable("false")) multiplexer_1 (
    .in0(x0_q), .in1(x1_q), .in2(x2_q), .in5(x5_q), .in6(x6_q), .in7(x7_q), .in8(x8_q), .in9(x9_q),
    .in10(x10_q), .out(Read_Data_1), .sel(rs1));  // open: in3, in4, in11, in12, in13, in14, in15, in16, in17, in18, in19, in20, in21, in22, in23, in24, in25, in26, in27, in28, in29, in30, in31
  Multiplexer #(.select(5), .width(32), .enable("false")) multiplexer_2 (
    .in0(x0_q), .in1(x1_q), .in2(x2_q), .in5(x5_q), .in6(x6_q), .in7(x7_q), .in8(x8_q), .in9(x9_q),
    .in10(x10_q), .out(Read_Data_2), .sel(rs2));  // open: in3, in4, in11, in12, in13, in14, in15, in16, in17, in18, in19, in20, in21, in22, in23, in24, in25, in26, in27, in28, in29, in30, in31

  // Notes on the sheet:
  //   Made by cs1221596 and cs1221094
endmodule
