// Logisim project processor.circ as structural Verilog
module main (
  input  Enable,
  input  Reset,
  output [4:0] rd,
  output [4:0] rs1,
  output [4:0] rs2,
  output [31:0] op1,
  output overflow,
  output [31:0] Rd2,
  output zero,
  output [31:0] result,
  output write,
  output sw,
  output lw,
  output [31:0] PC,
  output [31:0] Instruction,
  output [31:0] memory,
  output [31:0] Imm,
  output [31:0] op2,
  output [3:0] ALUOp
);

  wire and_1_out, clk, clk_out, decoder_circ_13759396_1_alusrc, decoder_circ_13759396_1_beq, lw_t, sw_t;
  wire [31:0] adder_1_out, adder_2_out, memory_t, multiplexer_2_out, multiplexer_3_out, ram_1_dout, Rd2_t;

  Clock u_clk (.out(clk_out));
  Register #(.width(32)) PCRegister (.D(multiplexer_3_out), .en(Enable), .clk(clk_out), .Q(PC), .clr(Reset));
  ROM #(.addrWidth(24), .dataWidth(32)) rom_1 (.addr(PC[25:2]), .data(Instruction));
  Adder #(.width(32)) adder_1 (.a(32'h4), .b(PC), .out(adder_1_out));  // open: cin, cout
  decoder_circ_13759396 decoder_circ_13759396_1 (
    .Instruction(Instruction), .ALUOp(ALUOp), .BEQ(decoder_circ_13759396_1_beq), .LW(lw), .rd(rd), .SW(sw),
    .ALUSrc(decoder_circ_13759396_1_alusrc), .rs1(rs1), .write(write), .rs2(rs2), .immediate(Imm));  // open: out_8
  register_circ_a9f9d4df register_circ_a9f9d4df_1 (
    .rs1(rs1), .rd(rd), .rs2(rs2), .Write_Data_d307f283(multiplexer_2_out), .RegWEn(write),
    .Read_Data_1_ed0725e9(op1), .Read_Data_2_04c6ea90(Rd2));
  Multiplexer #(.width(32)) multiplexer_1 (.in0(Imm), .in1(Rd2), .out(op2), .sel(decoder_circ_13759396_1_alusrc));
  Adder #(.width(32)) adder_2 (.a(PC), .b(Imm), .out(adder_2_out));  // open: cin, cout
  Multiplexer #(.width(32)) multiplexer_2 (.in0(result), .in1(memory_t), .out(multiplexer_2_out), .sel(lw_t));
  Multiplexer #(.width(32)) multiplexer_3 (
    .in0(adder_1_out), .in1(adder_2_out), .out(multiplexer_3_out), .sel(and_1_out));
  and and_1 (and_1_out, decoder_circ_13759396_1_beq, zero);
  alu_circ_95d0095d alu_circ_95d0095d_1 (
    .A(op1), .B(op2), .ALUSel(ALUOp), .Result(result), .overflow(overflow), .zero(zero));
  RAM_part #(.addrWidth(24), .dataWidth(32)) ram_1 (
    .addr(result[25:2]), .we(sw_t), .oe(lw_t), .clk(clk), .din(Rd2_t), .dout(ram_1_dout));
  Register #(.width(32)) register_1 (.D(ram_1_dout), .en(1'b1), .clk(clk), .Q(memory));  // open: clr

  // Notes on the sheet:
  //   contents of rom_1 (hex, n*v repeats v):
  //   5100b3 310093 405100b3 5110b3 5120b3 5130b3 5140b3 5150b3 5160b3 5170b3 312093 313093 314093 316093
  //   317093 12083 20a023 14730563
  //   cs1221094 and cs1221596
endmodule

// Decode Unit
module decoder_circ_13759396 (
  input  [31:0] Instruction,
  output [4:0] rd,
  output [3:0] ALUOp,
  output [4:0] rs1,
  output [4:0] rs2,
  output SW,
  output [31:0] immediate,
  output [11:0] out_8,
  output write,
  output BEQ,
  output LW,
  output ALUSrc
);

  wire comparator_1_eq, comparator_6_eq, or_3_out;
  wire [0:0] or_1_out;
  wire [3:0] multiplexer_2_out;
  wire [3:3] not_1_out;
  wire [11:0] multiplexer_1_out, shifter_1_out;

  Comparator #(.width(7)) comparator_1 (.a(7'b0010011), .b(Instruction[6:0]), .eq(comparator_1_eq));  // open: gt, lt
  Comparator #(.width(7)) comparator_2 (.a(Instruction[6:0]), .b(7'b0000011), .eq(LW));  // open: gt, lt
  Comparator #(.width(7)) comparator_3 (.a(Instruction[6:0]), .b(7'b1100011), .eq(BEQ));  // open: gt, lt
  Shifter #(.width(12)) shifter_1 (
    .in({Instruction[31], Instruction[7], Instruction[30:25], Instruction[11:8]}), .\dist (4'b0001),
    .out(shifter_1_out));
  Comparator #(.width(7)) comparator_4 (.a(7'b0110011), .b(Instruction[6:0]), .eq(ALUSrc));  // open: gt, lt
  Comparator #(.width(7)) comparator_5 (.a(Instruction[6:0]), .b(7'b0100011), .eq(SW));  // open: gt, lt
  or or_1 (or_1_out[0], comparator_1_eq, LW);
  or or_2 (write, or_1_out[0], ALUSrc);
  Multiplexer #(.select(3), .width(12)) multiplexer_1 (
    .in0({12{1'b0}}), .in1(Instruction[31:20]), .in2({Instruction[31:25], Instruction[11:7]}),
    .in3({12{1'b0}}), .in4(shifter_1_out), .in5({12{1'b0}}), .in6({12{1'b0}}), .in7({12{1'b0}}),
    .out(multiplexer_1_out), .sel({BEQ, SW, or_1_out[0]}));
  not not_1 (not_1_out[3], comparator_6_eq);
  Comparator #(.width(7)) comparator_6 (
    .a({7{1'b0}}),
    .b({Instruction[25], Instruction[26], Instruction[27], Instruction[28], Instruction[29], Instruction[30], Instruction[31]}),
    .eq(comparator_6_eq));  // open: gt, lt
  assign immediate = {{20{1'b0}}, multiplexer_1_out};  // Bit_Extender bit_extender_1
  Multiplexer #(.width(4)) multiplexer_2 (.in0(4'b0010), .in1(4'b0000), .out(multiplexer_2_out), .sel(or_3_out));
  or or_3 (or_3_out, SW, LW);
  Multiplexer #(.select(4), .width(4)) multiplexer_3 (
    .in0(4'b0000), .in1(4'b0001), .in2(multiplexer_2_out), .in3(4'b0011), .in4(4'b0100), .in5(4'b0101),
    .in6(4'b0110), .in7(4'b0111), .in8(4'b1100), .out(ALUOp), .sel({not_1_out[3], Instruction[14:12]}));  // open: in9, in10, in11, in12, in13, in14, in15

  assign out_8 = {Instruction[31:25], Instruction[11:7]};
  assign rd = Instruction[11:7];
  assign rs1 = Instruction[19:15];
  assign rs2 = Instruction[24:20];

  // Notes on the sheet:
  //   opcode
  //   other than lw i-instrn
  //   lw instruction
  //   s-type immediate
  //   funct3
  //   funct7
  //   R-type -> ALUSrc = 1 else 0;
  //   WE is 1 for all I and R -type instructions
endmodule

// Reg
module register_circ_a9f9d4df (
  input  [4:0] rd,
  input  [31:0] Write_Data_d307f283,
  input  RegWEn,
  input  [4:0] rs1,
  input  [4:0] rs2,
  output [31:0] Read_Data_1_ed0725e9,
  output [31:0] Read_Data_2_04c6ea90
);

  wire and_1_out, and_2_out, and_3_out, and_4_out, and_5_out, and_6_out, and_7_out, and_8_out, clock_1_out,
       decoder_1_out1, decoder_1_out2, decoder_1_out5, decoder_1_out6, decoder_1_out7, decoder_1_out8,
       decoder_1_out9, decoder_1_out10;
  wire [31:0] x0_q, x1_q, x2_q, x5_q, x6_q, x7_q, x8_q, x9_q, x10_q;

  Decoder #(.enable("false"), .select(5)) decoder_1 (
    .out1(decoder_1_out1), .out2(decoder_1_out2), .out5(decoder_1_out5), .out6(decoder_1_out6),
    .out7(decoder_1_out7), .out8(decoder_1_out8), .out9(decoder_1_out9), .out10(decoder_1_out10), .sel(rd));  // open: out0, out3, out4, out11, out12, out13, out14, out15, out16, out17, out18, out19, out20, out21, out22, out23, out24, out25, out26, out27, out28, out29, out30, out31
  Clock clock_1 (.out(clock_1_out));
  and and_1 (and_1_out, RegWEn, decoder_1_out1);
  and and_2 (and_2_out, RegWEn, decoder_1_out2);
  and and_3 (and_3_out, RegWEn, decoder_1_out5);
  and and_4 (and_4_out, RegWEn, decoder_1_out6);
  and and_5 (and_5_out, RegWEn, decoder_1_out7);
  and and_6 (and_6_out, RegWEn, decoder_1_out8);
  and and_7 (and_7_out, RegWEn, decoder_1_out9);
  and and_8 (and_8_out, RegWEn, decoder_1_out10);
  Register #(.width(32)) x0 (.D(Write_Data_d307f283), .en(1'b0), .Q(x0_q), .clk(clock_1_out));  // open: clr
  Register #(.width(32)) x1 (.D(Write_Data_d307f283), .en(and_1_out), .Q(x1_q), .clk(clock_1_out));  // open: clr
  Register #(.width(32)) x2 (.D(Write_Data_d307f283), .en(and_2_out), .Q(x2_q), .clk(clock_1_out));  // open: clr
  Register #(.width(32)) x5 (.D(Write_Data_d307f283), .en(and_3_out), .Q(x5_q), .clk(clock_1_out));  // open: clr
  Register #(.width(32)) x6 (.D(Write_Data_d307f283), .en(and_4_out), .Q(x6_q), .clk(clock_1_out));  // open: clr
  Register #(.width(32)) x7 (.D(Write_Data_d307f283), .en(and_5_out), .Q(x7_q), .clk(clock_1_out));  // open: clr
  Register #(.width(32)) x8 (.D(Write_Data_d307f283), .en(and_6_out), .Q(x8_q), .clk(clock_1_out));  // open: clr
  Register #(.width(32)) x9 (.D(Write_Data_d307f283), .en(and_7_out), .Q(x9_q), .clk(clock_1_out));  // open: clr
  Register #(.width(32)) x10 (.D(Write_Data_d307f283), .en(and_8_out), .Q(x10_q), .clk(clock_1_out));  // open: clr
  Multiplexer #(.select(5), .width(32)) multiplexer_1 (
    .in0(x0_q), .in1(x1_q), .in2(x2_q), .in3({32{1'b0}}), .in4({32{1'b0}}), .in5(x5_q), .in6(x6_q),
    .in7(x7_q), .in8(x8_q), .in9(x9_q), .in10(x10_q), .in11({32{1'b0}}), .in12({32{1'b0}}),
    .in13({32{1'b0}}), .in14({32{1'b0}}), .in15({32{1'b0}}), .in16({32{1'b0}}), .in17({32{1'b0}}),
    .in18({32{1'b0}}), .in19({32{1'b0}}), .in20({32{1'b0}}), .in21({32{1'b0}}), .in22({32{1'b0}}),
    .in23({32{1'b0}}), .in24({32{1'b0}}), .in25({32{1'b0}}), .in26({32{1'b0}}), .in27({32{1'b0}}),
    .in28({32{1'b0}}), .in29({32{1'b0}}), .in30({32{1'b0}}), .in31({32{1'b0}}), .out(Read_Data_1_ed0725e9),
    .sel(rs1));
  Multiplexer #(.select(5), .width(32)) multiplexer_2 (
    .in0(x0_q), .in1(x1_q), .in2(x2_q), .in3({32{1'b0}}), .in4({32{1'b0}}), .in5(x5_q), .in6(x6_q),
    .in7(x7_q), .in8(x8_q), .in9(x9_q), .in10(x10_q), .in11({32{1'b0}}), .in12({32{1'b0}}),
    .in13({32{1'b0}}), .in14({32{1'b0}}), .in15({32{1'b0}}), .in16({32{1'b0}}), .in17({32{1'b0}}),
    .in18({32{1'b0}}), .in19({32{1'b0}}), .in20({32{1'b0}}), .in21({32{1'b0}}), .in22({32{1'b0}}),
    .in23({32{1'b0}}), .in24({32{1'b0}}), .in25({32{1'b0}}), .in26({32{1'b0}}), .in27({32{1'b0}}),
    .in28({32{1'b0}}), .in29({32{1'b0}}), .in30({32{1'b0}}), .in31({32{1'b0}}), .out(Read_Data_2_04c6ea90),
    .sel(rs2));

  // Notes on the sheet:
  //   Made by cs1221596 and cs1221094
endmodule

// ALU
module alu_circ_95d0095d (
  input  [31:0] A,
  input  [31:0] B,
  input  [3:0] ALUSel,
  output overflow,
  output zero,
  output [31:0] Result
);

  control_signal control_signal_1 (
    .in_1(A), .in_2(B), .ALUSel(ALUSel), .overflow(overflow), .zero(zero), .Result(Result));

  // Notes on the sheet:
  //   cs1221596 and cs1221094
endmodule

module add_0 (
  input  [30:0] A_30_0_bb82ce94,
  input  [30:0] B_30_0_97caf3aa,
  input  A_31_e4cafb7f,
  input  B_31_65d76240,
  output [31:0] Result,
  output Overflow
);

  wire [31:0] bit_extender_1_out, bit_extender_2_out;

  assign bit_extender_1_out = {{1{A_31_e4cafb7f}}, A_30_0_bb82ce94};  // Bit_Extender bit_extender_1
  assign bit_extender_2_out = {{1{B_31_65d76240}}, B_30_0_97caf3aa};  // Bit_Extender bit_extender_2
  Adder #(.width(32)) adder_1 (
    .a(bit_extender_1_out), .b(bit_extender_2_out), .out(Result), .cin(1'b0), .cout(Overflow));
endmodule

module sll_1 (
  input  [30:0] A_30_0_bb82ce94,
  input  [30:0] B_30_0_97caf3aa,
  input  A_31_e4cafb7f,
  input  B_31_65d76240,
  output [31:0] Result
);

  wire bitfinder_1_found;
  wire [4:0] bitselector_1_out;
  wire [31:0] bit_extender_1_out, bit_extender_2_out, shifter_1_out;

  assign bit_extender_1_out = {{1{A_31_e4cafb7f}}, A_30_0_bb82ce94};  // Bit_Extender bit_extender_1
  assign bit_extender_2_out = {{1{B_31_65d76240}}, B_30_0_97caf3aa};  // Bit_Extender bit_extender_2
  BitSelector #(.group(5), .width(32)) bitselector_1 (.in(bit_extender_2_out), .out(bitselector_1_out), .sel(3'b000));
  BitFinder #(.width(27)) bitfinder_1 (.in(bit_extender_2_out[31:5]), .found(bitfinder_1_found));  // open: index
  Shifter #(.width(32)) shifter_1 (.in(bit_extender_1_out), .\dist (bitselector_1_out), .out(shifter_1_out));
  MUX_32bit_2_1_95e4f4e7 mux_32bit_2_1_95e4f4e7_1 (
    .in_1(shifter_1_out), .in_2({32{1'b0}}), .in_3(bitfinder_1_found), .out_4(Result));
endmodule

module slt_2 (
  input  [30:0] A_30_0_bb82ce94,
  input  [30:0] B_30_0_97caf3aa,
  input  A_31_e4cafb7f,
  input  B_31_65d76240,
  output [31:0] Result
);

  wire comparator_1_lt;
  wire [31:0] bit_extender_1_out, bit_extender_2_out;

  assign bit_extender_1_out = {{1{A_31_e4cafb7f}}, A_30_0_bb82ce94};  // Bit_Extender bit_extender_1
  assign bit_extender_2_out = {{1{B_31_65d76240}}, B_30_0_97caf3aa};  // Bit_Extender bit_extender_2
  Comparator #(.width(32)) comparator_1 (
    .a(bit_extender_1_out), .b(bit_extender_2_out), .lt(comparator_1_lt));  // open: gt, eq
  assign Result = {{31{comparator_1_lt}}, comparator_1_lt};  // Bit_Extender bit_extender_3
endmodule

module xor_4 (
  input  [30:0] A_30_0_bb82ce94,
  input  [30:0] B_30_0_97caf3aa,
  input  A_31_e4cafb7f,
  input  B_31_65d76240,
  output [31:0] Result
);

  wire [31:0] bit_extender_1_out, bit_extender_2_out;

  assign bit_extender_1_out = {{1{A_31_e4cafb7f}}, A_30_0_bb82ce94};  // Bit_Extender bit_extender_1
  assign bit_extender_2_out = {{1{B_31_65d76240}}, B_30_0_97caf3aa};  // Bit_Extender bit_extender_2
  assign Result = bit_extender_1_out ^ bit_extender_2_out;  // XOR_Gate xor_1, 32 bits wide
endmodule

module srl_5 (
  input  [30:0] A_30_0_bb82ce94,
  input  [30:0] B_30_0_97caf3aa,
  input  A_31_e4cafb7f,
  input  B_31_65d76240,
  output [31:0] Result
);

  wire bitfinder_1_found;
  wire [4:0] bitselector_1_out;
  wire [31:0] bit_extender_1_out, bit_extender_2_out, shifter_1_out;

  assign bit_extender_1_out = {{1{A_31_e4cafb7f}}, A_30_0_bb82ce94};  // Bit_Extender bit_extender_1
  assign bit_extender_2_out = {{1{B_31_65d76240}}, B_30_0_97caf3aa};  // Bit_Extender bit_extender_2
  Shifter #(.shift("lr"), .width(32)) shifter_1 (
    .in(bit_extender_1_out), .\dist (bitselector_1_out), .out(shifter_1_out));
  BitSelector #(.group(5), .width(32)) bitselector_1 (.in(bit_extender_2_out), .out(bitselector_1_out), .sel(3'b000));
  BitFinder #(.width(27)) bitfinder_1 (.in(bit_extender_2_out[31:5]), .found(bitfinder_1_found));  // open: index
  MUX_32bit_2_1_95e4f4e7 mux_32bit_2_1_95e4f4e7_1 (
    .in_1(shifter_1_out), .in_2({32{1'b0}}), .in_3(bitfinder_1_found), .out_4(Result));
endmodule

module or_6 (
  input  [30:0] A_30_0_bb82ce94,
  input  [30:0] B_30_0_97caf3aa,
  input  A_31_e4cafb7f,
  input  B_31_65d76240,
  output [31:0] out_5
);

  wire [31:0] bit_extender_1_out, bit_extender_2_out;

  assign bit_extender_1_out = {{1{A_31_e4cafb7f}}, A_30_0_bb82ce94};  // Bit_Extender bit_extender_1
  assign bit_extender_2_out = {{1{B_31_65d76240}}, B_30_0_97caf3aa};  // Bit_Extender bit_extender_2
  assign out_5 = bit_extender_1_out | bit_extender_2_out;  // OR_Gate or_1, 32 bits wide
endmodule

module and_7 (
  input  [30:0] A_30_0_bb82ce94,
  input  [30:0] B_30_0_97caf3aa,
  input  A_31_e4cafb7f,
  input  B_31_65d76240,
  output [31:0] out_5
);

  wire [31:0] bit_extender_1_out, bit_extender_2_out;

  assign bit_extender_1_out = {{1{A_31_e4cafb7f}}, A_30_0_bb82ce94};  // Bit_Extender bit_extender_1
  assign bit_extender_2_out = {{1{B_31_65d76240}}, B_30_0_97caf3aa};  // Bit_Extender bit_extender_2
  assign out_5 = bit_extender_1_out & bit_extender_2_out;  // AND_Gate and_1, 32 bits wide
endmodule

module mul_8 (
  input  [30:0] A_30_0_bb82ce94,
  input  [30:0] B_30_0_97caf3aa,
  input  A_31_e4cafb7f,
  input  B_31_65d76240,
  output [31:0] Result
);

  wire [31:0] bit_extender_1_out, bit_extender_2_out;

  assign bit_extender_1_out = {{1{A_31_e4cafb7f}}, A_30_0_bb82ce94};  // Bit_Extender bit_extender_1
  assign bit_extender_2_out = {{1{B_31_65d76240}}, B_30_0_97caf3aa};  // Bit_Extender bit_extender_2
  Multiplier #(.width(32)) multiplier_1 (
    .a(bit_extender_1_out), .b(bit_extender_2_out), .out(Result), .cin({32{1'b0}}));  // open: cout
endmodule

module sub_12 (
  input  [30:0] A_30_0_bb82ce94,
  input  [30:0] B_30_0_97caf3aa,
  input  A_31_e4cafb7f,
  input  B_31_65d76240,
  output [31:0] Result
);

  wire [31:0] bit_extender_1_out, bit_extender_2_out;

  assign bit_extender_1_out = {{1{A_31_e4cafb7f}}, A_30_0_bb82ce94};  // Bit_Extender bit_extender_1
  assign bit_extender_2_out = {{1{B_31_65d76240}}, B_30_0_97caf3aa};  // Bit_Extender bit_extender_2
  Subtractor #(.width(32)) subtractor_1 (
    .a(bit_extender_1_out), .b(bit_extender_2_out), .out(Result), .bin(1'b0));  // open: bout
endmodule

module sra_13 (
  input  [30:0] A_30_0_bb82ce94,
  input  [30:0] B_30_0_97caf3aa,
  input  A_31_e4cafb7f,
  input  B_31_65d76240,
  output [31:0] Result
);

  wire bitfinder_1_found;
  wire [4:0] bitselector_1_out;
  wire [31:0] bit_extender_1_out, bit_extender_2_out, shifter_1_out;

  assign bit_extender_1_out = {{1{A_31_e4cafb7f}}, A_30_0_bb82ce94};  // Bit_Extender bit_extender_1
  assign bit_extender_2_out = {{1{B_31_65d76240}}, B_30_0_97caf3aa};  // Bit_Extender bit_extender_2
  BitSelector #(.group(5), .width(32)) bitselector_1 (.in(bit_extender_2_out), .out(bitselector_1_out), .sel(3'b000));
  BitFinder #(.width(27)) bitfinder_1 (.in(bit_extender_2_out[31:5]), .found(bitfinder_1_found));  // open: index
  Shifter #(.shift("ar"), .width(32)) shifter_1 (
    .in(bit_extender_1_out), .\dist (bitselector_1_out), .out(shifter_1_out));
  MUX_32bit_2_1_95e4f4e7 mux_32bit_2_1_95e4f4e7_1 (
    .in_1(shifter_1_out), .in_2({32{1'b0}}), .in_3(bitfinder_1_found), .out_4(Result));
endmodule

module bsel_15 (
  input  [30:0] A_30_0_bb82ce94,
  input  [30:0] B_30_0_97caf3aa,
  input  A_31_e4cafb7f,
  input  B_31_65d76240,
  output [31:0] Result
);

  assign Result = {{1{B_31_65d76240}}, B_30_0_97caf3aa};  // Bit_Extender bit_extender_1
endmodule

module splitter (
  input  [31:0] A,
  input  [31:0] B,
  output [30:0] A_30_0_bb82ce94,
  output [30:0] B_30_0_97caf3aa,
  output A_31_e4cafb7f,
  output B_31_65d76240
);


  assign A_30_0_bb82ce94 = A[30:0];
  assign A_31_e4cafb7f = A[31];
  assign B_30_0_97caf3aa = B[30:0];
  assign B_31_65d76240 = B[31];
endmodule

module MUX_32bit_2_1_95e4f4e7 (
  input  [31:0] in_1,
  input  [31:0] in_2,
  input  in_3,
  output [31:0] out_4
);

  wire [31:0] and_1_out, and_2_out, bit_extender_1_out, not_1_out;

  assign bit_extender_1_out = {{31{in_3}}, in_3};  // Bit_Extender bit_extender_1
  assign not_1_out = ~bit_extender_1_out;  // NOT_Gate not_1, 32 bits wide
  assign and_1_out = in_1 & not_1_out;  // AND_Gate and_1, 32 bits wide
  assign and_2_out = in_2 & bit_extender_1_out;  // AND_Gate and_2, 32 bits wide
  assign out_4 = and_1_out | and_2_out;  // OR_Gate or_1, 32 bits wide
endmodule

module L_2_s_complement_4b2b666a (
  input  [30:0] in_1,
  input  in_2,
  output [31:0] out_3
);

  wire [30:0] adder_1_out, bit_extender_1_out, bit_extender_2_out, xor_1_out;

  assign bit_extender_1_out = {{30{in_2}}, in_2};  // Bit_Extender bit_extender_1
  assign bit_extender_2_out = {{30{in_2}}, in_2};  // Bit_Extender bit_extender_2
  assign xor_1_out = in_1 ^ bit_extender_1_out;  // XOR_Gate xor_1, 31 bits wide
  assign out_3 = {{1{adder_1_out[30]}}, adder_1_out};  // Bit_Extender bit_extender_3
  Adder #(.width(31)) adder_1 (.a(xor_1_out), .b(bit_extender_2_out), .out(adder_1_out), .cin(1'b0));  // open: cout
endmodule

module MUX_1bit_2_1_0c3bf1c0 (
  input  in_1,
  input  in_2,
  input  in_3,
  output out_4
);

  wire and_1_out, and_2_out, not_1_out;

  not not_1 (not_1_out, in_3);
  and and_1 (and_1_out, in_1, not_1_out);
  and and_2 (and_2_out, in_2, in_3);
  or or_1 (out_4, and_1_out, and_2_out);
endmodule

module MUX_16_1_8b74caa0 (
  input  [31:0] L_0_49eb53ea,
  input  [31:0] L_8_2246fdba,
  input  [31:0] L_4_d7651adc,
  input  [31:0] L_12_295108df,
  input  [31:0] L_2_ac128e4b,
  input  [31:0] L_10_615d1d6f,
  input  [31:0] L_6_4325d025,
  input  [31:0] L_14_62f55a35,
  input  [31:0] L_1_b22af223,
  input  [31:0] L_9_6021bb78,
  input  [31:0] L_5_087e8c8a,
  input  [31:0] L_13_ffa99f69,
  input  [31:0] L_3_b6c1e611,
  input  [31:0] L_11_b7176902,
  input  [31:0] L_7_f4d1364a,
  input  [31:0] L_15_352d3321,
  input  [3:0] in_17,
  output [31:0] out_18
);

  wire [31:0] mux_32bit_2_1_95e4f4e7_1_out_4, mux_32bit_2_1_95e4f4e7_2_out_4, mux_32bit_2_1_95e4f4e7_3_out_4,
       mux_32bit_2_1_95e4f4e7_4_out_4, mux_32bit_2_1_95e4f4e7_5_out_4, mux_32bit_2_1_95e4f4e7_6_out_4,
       mux_32bit_2_1_95e4f4e7_7_out_4, mux_32bit_2_1_95e4f4e7_8_out_4, mux_32bit_2_1_95e4f4e7_9_out_4,
       mux_32bit_2_1_95e4f4e7_10_out_4, mux_32bit_2_1_95e4f4e7_11_out_4, mux_32bit_2_1_95e4f4e7_12_out_4,
       mux_32bit_2_1_95e4f4e7_13_out_4, mux_32bit_2_1_95e4f4e7_14_out_4;

  MUX_32bit_2_1_95e4f4e7 mux_32bit_2_1_95e4f4e7_1 (
    .in_1(L_0_49eb53ea), .in_2(L_8_2246fdba), .in_3(in_17[3]), .out_4(mux_32bit_2_1_95e4f4e7_1_out_4));
  MUX_32bit_2_1_95e4f4e7 mux_32bit_2_1_95e4f4e7_2 (
    .in_1(L_4_d7651adc), .in_2(L_12_295108df), .in_3(in_17[3]), .out_4(mux_32bit_2_1_95e4f4e7_2_out_4));
  MUX_32bit_2_1_95e4f4e7 mux_32bit_2_1_95e4f4e7_3 (
    .in_1(L_2_ac128e4b), .in_2(L_10_615d1d6f), .in_3(in_17[3]), .out_4(mux_32bit_2_1_95e4f4e7_3_out_4));
  MUX_32bit_2_1_95e4f4e7 mux_32bit_2_1_95e4f4e7_4 (
    .in_1(L_6_4325d025), .in_2(L_14_62f55a35), .in_3(in_17[3]), .out_4(mux_32bit_2_1_95e4f4e7_4_out_4));
  MUX_32bit_2_1_95e4f4e7 mux_32bit_2_1_95e4f4e7_5 (
    .in_1(L_1_b22af223), .in_2(L_9_6021bb78), .in_3(in_17[3]), .out_4(mux_32bit_2_1_95e4f4e7_5_out_4));
  MUX_32bit_2_1_95e4f4e7 mux_32bit_2_1_95e4f4e7_6 (
    .in_1(L_5_087e8c8a), .in_2(L_13_ffa99f69), .in_3(in_17[3]), .out_4(mux_32bit_2_1_95e4f4e7_6_out_4));
  MUX_32bit_2_1_95e4f4e7 mux_32bit_2_1_95e4f4e7_7 (
    .in_1(L_3_b6c1e611), .in_2(L_11_b7176902), .in_3(in_17[3]), .out_4(mux_32bit_2_1_95e4f4e7_7_out_4));
  MUX_32bit_2_1_95e4f4e7 mux_32bit_2_1_95e4f4e7_8 (
    .in_1(L_7_f4d1364a), .in_2(L_15_352d3321), .in_3(in_17[3]), .out_4(mux_32bit_2_1_95e4f4e7_8_out_4));
  MUX_32bit_2_1_95e4f4e7 mux_32bit_2_1_95e4f4e7_9 (
    .in_1(mux_32bit_2_1_95e4f4e7_1_out_4), .in_2(mux_32bit_2_1_95e4f4e7_2_out_4), .in_3(in_17[2]),
    .out_4(mux_32bit_2_1_95e4f4e7_9_out_4));
  MUX_32bit_2_1_95e4f4e7 mux_32bit_2_1_95e4f4e7_10 (
    .in_1(mux_32bit_2_1_95e4f4e7_3_out_4), .in_2(mux_32bit_2_1_95e4f4e7_4_out_4), .in_3(in_17[2]),
    .out_4(mux_32bit_2_1_95e4f4e7_10_out_4));
  MUX_32bit_2_1_95e4f4e7 mux_32bit_2_1_95e4f4e7_11 (
    .in_1(mux_32bit_2_1_95e4f4e7_5_out_4), .in_2(mux_32bit_2_1_95e4f4e7_6_out_4), .in_3(in_17[2]),
    .out_4(mux_32bit_2_1_95e4f4e7_11_out_4));
  MUX_32bit_2_1_95e4f4e7 mux_32bit_2_1_95e4f4e7_12 (
    .in_1(mux_32bit_2_1_95e4f4e7_7_out_4), .in_2(mux_32bit_2_1_95e4f4e7_8_out_4), .in_3(in_17[2]),
    .out_4(mux_32bit_2_1_95e4f4e7_12_out_4));
  MUX_32bit_2_1_95e4f4e7 mux_32bit_2_1_95e4f4e7_13 (
    .in_1(mux_32bit_2_1_95e4f4e7_9_out_4), .in_2(mux_32bit_2_1_95e4f4e7_10_out_4), .in_3(in_17[1]),
    .out_4(mux_32bit_2_1_95e4f4e7_13_out_4));
  MUX_32bit_2_1_95e4f4e7 mux_32bit_2_1_95e4f4e7_14 (
    .in_1(mux_32bit_2_1_95e4f4e7_11_out_4), .in_2(mux_32bit_2_1_95e4f4e7_12_out_4), .in_3(in_17[1]),
    .out_4(mux_32bit_2_1_95e4f4e7_14_out_4));
  MUX_32bit_2_1_95e4f4e7 mux_32bit_2_1_95e4f4e7_15 (
    .in_1(mux_32bit_2_1_95e4f4e7_13_out_4), .in_2(mux_32bit_2_1_95e4f4e7_14_out_4), .in_3(in_17[0]),
    .out_4(out_18));
endmodule

module control_signal (
  input  [31:0] in_1,
  input  [31:0] in_2,
  input  [3:0] ALUSel,
  output overflow,
  output zero,
  output [31:0] Result
);

  wire add_0_1_overflow, bitfinder_1_found, not_1_out, splitter_1_a_31_e4cafb7f, splitter_1_b_31_65d76240;
  wire [30:0] splitter_1_a_30_0_bb82ce94, splitter_1_b_30_0_97caf3aa;
  wire [31:0] add_0_1_result, and_7_1_out_5, bsel_15_1_result, mul_8_1_result, mulh_9_1_result, or_6_1_out_5,
       sll_1_1_result, slt_2_1_result, sltu_3_1_out_5, sra_13_1_result, srl_5_1_result, sub_12_1_result,
       undriven, xor_4_1_result;

  splitter splitter_1 (
    .A(in_1), .B(in_2), .A_30_0_bb82ce94(splitter_1_a_30_0_bb82ce94),
    .B_30_0_97caf3aa(splitter_1_b_30_0_97caf3aa), .A_31_e4cafb7f(splitter_1_a_31_e4cafb7f),
    .B_31_65d76240(splitter_1_b_31_65d76240));
  add_0 add_0_1 (
    .A_30_0_bb82ce94(splitter_1_a_30_0_bb82ce94), .B_30_0_97caf3aa(splitter_1_b_30_0_97caf3aa),
    .A_31_e4cafb7f(splitter_1_a_31_e4cafb7f), .B_31_65d76240(splitter_1_b_31_65d76240),
    .Overflow(add_0_1_overflow), .Result(add_0_1_result));
  mul_8 mul_8_1 (
    .A_30_0_bb82ce94(splitter_1_a_30_0_bb82ce94), .B_30_0_97caf3aa(splitter_1_b_30_0_97caf3aa),
    .A_31_e4cafb7f(splitter_1_a_31_e4cafb7f), .B_31_65d76240(splitter_1_b_31_65d76240),
    .Result(mul_8_1_result));
  xor_4 xor_4_1 (
    .A_30_0_bb82ce94(splitter_1_a_30_0_bb82ce94), .B_30_0_97caf3aa(splitter_1_b_30_0_97caf3aa),
    .A_31_e4cafb7f(splitter_1_a_31_e4cafb7f), .B_31_65d76240(splitter_1_b_31_65d76240),
    .Result(xor_4_1_result));
  sub_12 sub_12_1 (
    .A_30_0_bb82ce94(splitter_1_a_30_0_bb82ce94), .B_30_0_97caf3aa(splitter_1_b_30_0_97caf3aa),
    .A_31_e4cafb7f(splitter_1_a_31_e4cafb7f), .B_31_65d76240(splitter_1_b_31_65d76240),
    .Result(sub_12_1_result));
  slt_2 slt_2_1 (
    .A_30_0_bb82ce94(splitter_1_a_30_0_bb82ce94), .B_30_0_97caf3aa(splitter_1_b_30_0_97caf3aa),
    .A_31_e4cafb7f(splitter_1_a_31_e4cafb7f), .B_31_65d76240(splitter_1_b_31_65d76240),
    .Result(slt_2_1_result));
  or_6 or_6_1 (
    .A_30_0_bb82ce94(splitter_1_a_30_0_bb82ce94), .B_30_0_97caf3aa(splitter_1_b_30_0_97caf3aa),
    .A_31_e4cafb7f(splitter_1_a_31_e4cafb7f), .B_31_65d76240(splitter_1_b_31_65d76240), .out_5(or_6_1_out_5));
  sll_1 sll_1_1 (
    .A_30_0_bb82ce94(splitter_1_a_30_0_bb82ce94), .B_30_0_97caf3aa(splitter_1_b_30_0_97caf3aa),
    .A_31_e4cafb7f(splitter_1_a_31_e4cafb7f), .B_31_65d76240(splitter_1_b_31_65d76240),
    .Result(sll_1_1_result));
  mulh_9 mulh_9_1 (
    .A_30_0_bb82ce94(splitter_1_a_30_0_bb82ce94), .B_30_0_97caf3aa(splitter_1_b_30_0_97caf3aa),
    .A_31_e4cafb7f(splitter_1_a_31_e4cafb7f), .B_31_65d76240(splitter_1_b_31_65d76240),
    .Result(mulh_9_1_result));
  srl_5 srl_5_1 (
    .A_30_0_bb82ce94(splitter_1_a_30_0_bb82ce94), .B_30_0_97caf3aa(splitter_1_b_30_0_97caf3aa),
    .A_31_e4cafb7f(splitter_1_a_31_e4cafb7f), .B_31_65d76240(splitter_1_b_31_65d76240),
    .Result(srl_5_1_result));
  sra_13 sra_13_1 (
    .A_30_0_bb82ce94(splitter_1_a_30_0_bb82ce94), .B_30_0_97caf3aa(splitter_1_b_30_0_97caf3aa),
    .A_31_e4cafb7f(splitter_1_a_31_e4cafb7f), .B_31_65d76240(splitter_1_b_31_65d76240),
    .Result(sra_13_1_result));
  sltu_3 sltu_3_1 (
    .A_30_0_bb82ce94(splitter_1_a_30_0_bb82ce94), .B_30_0_97caf3aa(splitter_1_b_30_0_97caf3aa),
    .A_31_e4cafb7f(splitter_1_a_31_e4cafb7f), .B_31_65d76240(splitter_1_b_31_65d76240), .out_5(sltu_3_1_out_5));
  mulhu_11 mulhu_11_1 ();
  and_7 and_7_1 (
    .A_30_0_bb82ce94(splitter_1_a_30_0_bb82ce94), .B_30_0_97caf3aa(splitter_1_b_30_0_97caf3aa),
    .A_31_e4cafb7f(splitter_1_a_31_e4cafb7f), .B_31_65d76240(splitter_1_b_31_65d76240), .out_5(and_7_1_out_5));
  bsel_15 bsel_15_1 (
    .A_30_0_bb82ce94(splitter_1_a_30_0_bb82ce94), .B_30_0_97caf3aa(splitter_1_b_30_0_97caf3aa),
    .A_31_e4cafb7f(splitter_1_a_31_e4cafb7f), .B_31_65d76240(splitter_1_b_31_65d76240),
    .Result(bsel_15_1_result));
  MUX_16_1_8b74caa0 mux_16_1_8b74caa0_1 (
    .L_0_49eb53ea(add_0_1_result), .L_8_2246fdba(mul_8_1_result), .L_4_d7651adc(xor_4_1_result),
    .L_12_295108df(sub_12_1_result), .L_2_ac128e4b(slt_2_1_result), .L_10_615d1d6f({32{1'b0}}),
    .L_6_4325d025(or_6_1_out_5), .L_14_62f55a35({32{1'b0}}), .L_1_b22af223(sll_1_1_result),
    .L_9_6021bb78(mulh_9_1_result), .L_5_087e8c8a(srl_5_1_result), .L_13_ffa99f69(sra_13_1_result),
    .L_3_b6c1e611(sltu_3_1_out_5), .L_11_b7176902(undriven), .L_7_f4d1364a(and_7_1_out_5),
    .L_15_352d3321(bsel_15_1_result), .in_17(ALUSel), .out_18(Result));
  BitFinder #(.\type ("high1"), .width(4)) bitfinder_1 (.in(ALUSel), .found(bitfinder_1_found));  // open: index
  and and_1 (overflow, add_0_1_overflow, not_1_out);
  not not_1 (not_1_out, bitfinder_1_found);
  Comparator #(.width(32)) comparator_1 (.a(Result), .b({32{1'b0}}), .eq(zero));  // open: gt, lt
endmodule

module mulh_9 (
  input  [30:0] A_30_0_bb82ce94,
  input  [30:0] B_30_0_97caf3aa,
  input  A_31_e4cafb7f,
  input  B_31_65d76240,
  output [31:0] Result
);

  wire [31:0] bit_extender_1_out, bit_extender_2_out;

  assign bit_extender_1_out = {{1{A_31_e4cafb7f}}, A_30_0_bb82ce94};  // Bit_Extender bit_extender_1
  assign bit_extender_2_out = {{1{B_31_65d76240}}, B_30_0_97caf3aa};  // Bit_Extender bit_extender_2
  Multiplier #(.width(32)) multiplier_1 (
    .a(bit_extender_1_out), .b(bit_extender_2_out), .cin({32{1'b0}}), .cout(Result));  // open: out
endmodule

module sltu_3 (
  input  [30:0] A_30_0_bb82ce94,
  input  [30:0] B_30_0_97caf3aa,
  input  A_31_e4cafb7f,
  input  B_31_65d76240,
  output [31:0] out_5
);

  wire comparator_1_lt;
  wire [31:0] bit_extender_1_out, bit_extender_2_out;

  assign bit_extender_1_out = {{1{A_31_e4cafb7f}}, A_30_0_bb82ce94};  // Bit_Extender bit_extender_1
  assign bit_extender_2_out = {{1{B_31_65d76240}}, B_30_0_97caf3aa};  // Bit_Extender bit_extender_2
  Comparator #(.mode("unsigned"), .width(32)) comparator_1 (
    .a(bit_extender_1_out), .b(bit_extender_2_out), .lt(comparator_1_lt));  // open: gt, eq
  assign out_5 = {{31{comparator_1_lt}}, comparator_1_lt};  // Bit_Extender bit_extender_3
endmodule

module RAM (
);

  RAM_part #(.addrWidth(24), .dataWidth(32)) ram_1 ();  // open: addr, we, oe, clk, din, dout
endmodule
